# Fritzing sketch spark-neopixel-external-5v (saved by Fritzing 0.9.0b)
breadboards: 1

parts:
  Part1 = Spark Core (v1.0)
  NEOPIXEL1 = Neopixel Strip -- White (60/m)
  JACK1 = 2.1mm Barrel Jack with Terminal Block
  C1 = Electrolytic Capacitor [capacitance=1000μF package="1010 [SMD, electrolytic]"]
  R1 = Resistor [tolerance=±5% resistance=220 package=THT]
  U1 = 74HC04_HEX_INVERTER [package=dil14]

nets:
  GND: Part1.GND, NEOPIXEL1.GND, JACK1.NEG, C1.-, U1.1A, U1.GND
  VIN: Part1.VIN, NEOPIXEL1.DI, JACK1.POS, C1.+, U1.VCC
  N1: Part1.D2, R1.Pin_1
  N2: NEOPIXEL1.+5V, U1.2A
  N3: R1.Pin_0, U1.1Y

notes:
  IMPORTANT
  The 74HC04 chip should actually be
  74AHCT125
  Capacitor should be at least 1000 µF, 6.3V
  Resistor should be between 300 and 500 ohm

custom parts:
  Neopixel Strip -- White (60/m): Neopixel Strip, White, 60 pixels per meter.
