# Fritzing sketch spark-neopixel-usb (saved by Fritzing 0.9.0b)
breadboards: 1

parts:
  Part1 = Spark Core (v1.0)
  R1 = Resistor [tolerance=±5% resistance=220 package=THT]
  NEOPIXEL1 = Neopixel Strip -- White (60/m)

nets:
  GND: Part1.GND, NEOPIXEL1.GND
  N1: Part1.VIN, NEOPIXEL1.DI
  N2: Part1.D2, R1.Pin_1
  N3: R1.Pin_0, NEOPIXEL1.+5V

notes:
  Powered from Spark USB

custom parts:
  Neopixel Strip -- White (60/m): Neopixel Strip, White, 60 pixels per meter.
